# Fritzing sketch bfc3000 (saved by Fritzing 0.9.2b)
perfboards: 1

parts:
  Part1 = OpenLog
  Tiny_RTC1 = Tiny RTC
  PIR1 = PIR sensor
  U1 = atmega328 [package=dip]
  Part2 = VERTER 5V USB Buck-Boost
  JP1 = Header 6 [package=1x06_smd_straight_alt]
  JP2 = Header 8 [package=1x08_smd_alt]  # not connected

nets (from the breadboard view):
  N1: Part1.RXI, U1.D0_(RX), JP1.2
  VCC: Part1.VCC, Tiny_RTC1.VCC, U1.VCC, Part2.5.0V, JP1.4
  GND: Part1.GND, Tiny_RTC1.GND, PIR1.GND, U1.GND#21, Part2.GND, JP1.5
  N2: Tiny_RTC1.SCL, U1.A5
  N3: Tiny_RTC1.SDA, U1.A4
  N4: PIR1.SIG, U1.D2

custom parts:
  Tiny RTC: Tiny RTC I2C module DS1370Z RTC and AT24C32 EEPROM
  VERTER 5V USB Buck-Boost: VERTER can take battery voltages from 3-12VDC and output a nice 5V DC, which makes it a perfect universal power supply for your portable project! Where Verter really shines is when you have a battery or power range that can fluctuate a lot, or you don't know what you'll end up using.
