# Fritzing sketch bfc3000_atmega328 (saved by Fritzing 0.9.2b)
perfboards: 1

parts:
  Part1 = OpenLog
  Tiny_RTC1 = Tiny RTC
  PIR1 = PIR sensor
  U1 = atmega328 [package=dip]
  JP1 = Header 6 [package=1x06_smd_straight_alt]
  JP2 = Header 8 [package=1x08_smd_alt]  # not connected
  JP3 = Header 1 [package=1x01_offset]
  JP4 = Header 1 [package=1x01_offset]
  JP5 = Header 1 [package=1x01_offset]
  JP6 = Header 1 [package=1x01_offset]
  JP7 = Header 1 [package=1x01_offset]
  JP8 = Header 1 [package=1x01_offset]
  C1 = Ceramic Capacitor [capacitance=100nF package="200 mil [THT, multilayer]"]
  BAT1 = BATTERY-2 [package=battery-aa]
  Part2 = VERTER 5V USB Buck-Boost

nets (from the breadboard view):
  N1: Part1.RXI, U1.D0_(RX), JP1.2
  VCC: Part1.VCC, Tiny_RTC1.VCC, U1.VCC, JP1.4, JP3.1, C1.0, Part2.5.0V
  GND: Part1.GND, Tiny_RTC1.GND, PIR1.GND, U1.GND#21, JP1.5, JP5.1, C1.1, BAT1.-1, Part2.GND
  N2: Tiny_RTC1.SCL, U1.A5
  N3: Tiny_RTC1.SDA, U1.A4
  N4: PIR1.SIG, U1.D2
  N5: U1.RESET, JP8.1
  N6: U1.D11_(PWM), JP4.1
  N7: U1.D12, JP6.1
  N8: U1.D13, JP7.1
  N9: BAT1.+1, Part2.VIN

notes:
  Cheap boost takes 1.2 V from battery

custom parts:
  Tiny RTC: Tiny RTC I2C module DS1370Z RTC and AT24C32 EEPROM
  VERTER 5V USB Buck-Boost: VERTER can take battery voltages from 3-12VDC and output a nice 5V DC, which makes it a perfect universal power supply for your portable project! Where Verter really shines is when you have a battery or power range that can fluctuate a lot, or you don't know what you'll end up using.
