# Fritzing sketch bfc3000_wemos (saved by Fritzing 0.9.2b)

parts:
  WeMos_D1_Mini1 = WeMos D1 Mini
  WeMos_D1_Mini_Micro_SD_Shield1 = WeMos D1 Mini Micro SD Shield
  WeMos_D1_Mini_Protoboard_Shield1 = WeMos D1 Mini Protoboard Shield
  WeMos_D1_Mini_Battery_Shield1 = WeMos D1 Mini Battery Shield
  PIR1 = PIR sensor

nets:
  3V3: WeMos_D1_Mini1.3V3, WeMos_D1_Mini_Micro_SD_Shield1.3V3
  5V: WeMos_D1_Mini1.5V, WeMos_D1_Mini_Protoboard_Shield1.5V, WeMos_D1_Mini_Protoboard_Shield1.X7-Y8, WeMos_D1_Mini_Battery_Shield1.5V, PIR1.VDD
  N1: WeMos_D1_Mini1.D1, WeMos_D1_Mini_Protoboard_Shield1.D1, WeMos_D1_Mini_Protoboard_Shield1.X7-Y3, PIR1.SIG
  N2: WeMos_D1_Mini1.D5, WeMos_D1_Mini_Micro_SD_Shield1.D5
  N3: WeMos_D1_Mini1.D6, WeMos_D1_Mini_Micro_SD_Shield1.D6
  N4: WeMos_D1_Mini1.D7, WeMos_D1_Mini_Micro_SD_Shield1.D7
  N5: WeMos_D1_Mini1.D8, WeMos_D1_Mini_Micro_SD_Shield1.D8
  N6: WeMos_D1_Mini1.G, WeMos_D1_Mini_Micro_SD_Shield1.G, WeMos_D1_Mini_Protoboard_Shield1.G, WeMos_D1_Mini_Protoboard_Shield1.X7-Y7, WeMos_D1_Mini_Battery_Shield1.G, PIR1.GND

notes:
  battery shield's
  power connector to solar lamp circuit
